// Logisim project cpu.circ as structural Verilog: 13 circuits, main circuit HalfAdder
module HalfAdder (
  input  A,
  input  B,
  output S,
  output C
);

  xor xor_1 (S, A, B);
  and and_1 (C, A, B);
endmodule

module FullAdder (
  input  A,
  input  B,
  input  C_in,
  output S,
  output C_out
);

  wire halfadder_1_c, halfadder_1_s, halfadder_2_c;

  HalfAdder halfadder_1 (.A(A), .B(B), .S(halfadder_1_s), .C(halfadder_1_c));
  HalfAdder halfadder_2 (.A(halfadder_1_s), .B(C_in), .S(S), .C(halfadder_2_c));
  or or_1 (C_out, halfadder_1_c, halfadder_2_c);
endmodule

module Adder8Sub (
  input  [7:0] A,
  input  [7:0] B,
  input  SUBTRACT,
  output [7:0] S,
  output OVERFLOW
);

  wire fulladder_1_c_out, fulladder_2_c_out, fulladder_3_c_out, fulladder_4_c_out, fulladder_5_c_out,
       fulladder_6_c_out, fulladder_7_c_out, xor_1_out, xor_2_out, xor_3_out, xor_4_out, xor_5_out,
       xor_6_out, xor_7_out, xor_8_out;

  xor xor_1 (xor_1_out, B[0], SUBTRACT);
  xor xor_2 (xor_2_out, B[1], SUBTRACT);
  xor xor_3 (xor_3_out, B[2], SUBTRACT);
  xor xor_4 (xor_4_out, B[3], SUBTRACT);
  xor xor_5 (xor_5_out, B[4], SUBTRACT);
  xor xor_6 (xor_6_out, B[5], SUBTRACT);
  xor xor_7 (xor_7_out, B[6], SUBTRACT);
  xor xor_8 (xor_8_out, B[7], SUBTRACT);
  FullAdder fulladder_1 (.A(A[0]), .B(xor_1_out), .C_in(SUBTRACT), .S(S[0]), .C_out(fulladder_1_c_out));
  FullAdder fulladder_2 (.A(A[1]), .B(xor_2_out), .C_in(fulladder_1_c_out), .S(S[1]), .C_out(fulladder_2_c_out));
  FullAdder fulladder_3 (.A(A[2]), .B(xor_3_out), .C_in(fulladder_2_c_out), .S(S[2]), .C_out(fulladder_3_c_out));
  FullAdder fulladder_4 (.A(A[3]), .B(xor_4_out), .C_in(fulladder_3_c_out), .S(S[3]), .C_out(fulladder_4_c_out));
  FullAdder fulladder_5 (.A(A[4]), .B(xor_5_out), .C_in(fulladder_4_c_out), .S(S[4]), .C_out(fulladder_5_c_out));
  FullAdder fulladder_6 (.A(A[5]), .B(xor_6_out), .C_in(fulladder_5_c_out), .S(S[5]), .C_out(fulladder_6_c_out));
  FullAdder fulladder_7 (.A(A[6]), .B(xor_7_out), .C_in(fulladder_6_c_out), .S(S[6]), .C_out(fulladder_7_c_out));
  FullAdder fulladder_8 (.A(A[7]), .B(xor_8_out), .C_in(fulladder_7_c_out), .S(S[7]), .C_out(OVERFLOW));

  // Other names for the same wires on the sheet: SUB = SUBTRACT
endmodule

module Comparator1 (
  input  A,
  input  B,
  output AEB,
  output ALB,
  output AGB
);

  xnor xnor_1 (AEB, A, B);
  and and_1 (ALB, ~A, B);  // AND_Gate
  and and_2 (AGB, A, ~B);  // AND_Gate
endmodule

module Comparator1C (
  input  A,
  input  B,
  input  AEBI,
  input  ALBI,
  input  AGBI,
  output AEBO,
  output ALBO,
  output AGBO
);

  wire and_1_out, and_2_out, comparator1_1_aeb, comparator1_1_agb, comparator1_1_alb;

  Comparator1 comparator1_1 (.A(A), .B(B), .AEB(comparator1_1_aeb), .ALB(comparator1_1_alb), .AGB(comparator1_1_agb));
  and and_1 (and_1_out, comparator1_1_aeb, ALBI);
  and and_2 (and_2_out, comparator1_1_aeb, AGBI);
  and and_3 (AEBO, comparator1_1_aeb, AEBI);
  or or_1 (ALBO, comparator1_1_alb, and_1_out);
  or or_2 (AGBO, comparator1_1_agb, and_2_out);
endmodule

module Comparator4C (
  input  AEBI,
  input  ALBI,
  input  AGBI,
  input  [3:0] A,
  input  [3:0] B,
  output AEBO,
  output ALBO,
  output AGBO
);

  wire comparator1c_1_aebo, comparator1c_1_agbo, comparator1c_1_albo, comparator1c_2_aebo,
       comparator1c_2_agbo, comparator1c_2_albo, comparator1c_3_aebo, comparator1c_3_agbo,
       comparator1c_3_albo;

  Comparator1C comparator1c_1 (
    .A(A[0]), .B(B[0]), .AEBI(AEBI), .ALBI(ALBI), .AGBI(AGBI), .AEBO(comparator1c_1_aebo),
    .ALBO(comparator1c_1_albo), .AGBO(comparator1c_1_agbo));
  Comparator1C comparator1c_2 (
    .A(A[1]), .B(B[1]), .AEBI(comparator1c_1_aebo), .ALBI(comparator1c_1_albo), .AGBI(comparator1c_1_agbo),
    .AEBO(comparator1c_2_aebo), .ALBO(comparator1c_2_albo), .AGBO(comparator1c_2_agbo));
  Comparator1C comparator1c_3 (
    .A(A[2]), .B(B[2]), .AEBI(comparator1c_2_aebo), .ALBI(comparator1c_2_albo), .AGBI(comparator1c_2_agbo),
    .AEBO(comparator1c_3_aebo), .ALBO(comparator1c_3_albo), .AGBO(comparator1c_3_agbo));
  Comparator1C comparator1c_4 (
    .A(A[3]), .B(B[3]), .AEBI(comparator1c_3_aebo), .ALBI(comparator1c_3_albo), .AGBI(comparator1c_3_agbo),
    .AEBO(AEBO), .ALBO(ALBO), .AGBO(AGBO));
endmodule

module Comparator8 (
  input  [7:0] A,
  input  [7:0] B,
  output AEBO,
  output ALBO,
  output AGBO
);

  wire comparator4c_1_aebo, comparator4c_1_agbo, comparator4c_1_albo;

  Comparator4C comparator4c_1 (
    .AEBI(1'b1), .ALBI(1'b0), .AGBI(1'b0), .A(A[3:0]), .B(B[3:0]), .AEBO(comparator4c_1_aebo),
    .ALBO(comparator4c_1_albo), .AGBO(comparator4c_1_agbo));
  Comparator4C comparator4c_2 (
    .AEBI(comparator4c_1_aebo), .ALBI(comparator4c_1_albo), .AGBI(comparator4c_1_agbo), .A(A[7:4]),
    .B(B[7:4]), .AEBO(AEBO), .ALBO(ALBO), .AGBO(AGBO));
endmodule

module MUX8 (
  input  [7:0] D0,
  input  [7:0] D1,
  input  S,
  output [7:0] Q
);

  wire [7:0] and_1_out, and_2_out, bit_extender_1_out;

  assign bit_extender_1_out = {{7{S}}, S};  // Bit_Extender bit_extender_1
  assign and_1_out = D0 & ~bit_extender_1_out;  // AND_Gate and_1, 8 bits wide
  assign and_2_out = bit_extender_1_out & D1;  // AND_Gate and_2, 8 bits wide
  assign Q = and_1_out | and_2_out;  // OR_Gate or_1, 8 bits wide
endmodule

module ALU8 (
  input  [7:0] X,
  input  [7:0] Y,
  input  [3:0] OPCODE,
  output STATUS,
  output [7:0] R
);

  wire AEBO, AGBO, ALBO, and_1_out, and_2_out, and_3_out, or_1_out;
  wire [7:0] adder8sub_1_s, bit_extender_1_out;

  and and_1 (and_1_out, AEBO, OPCODE[0]);
  and and_2 (and_2_out, ALBO, OPCODE[1]);
  and and_3 (and_3_out, AGBO, OPCODE[2]);
  or or_1 (or_1_out, and_1_out, and_2_out, and_3_out);
  Adder8Sub adder8sub_1 (.A(X), .B(Y), .SUBTRACT(OPCODE[0]), .S(adder8sub_1_s), .OVERFLOW(STATUS));
  Comparator8 comparator8_1 (.A(X), .B(Y), .AEBO(AEBO), .ALBO(ALBO), .AGBO(AGBO));
  MUX8 mux8_1 (.D0(adder8sub_1_s), .D1(bit_extender_1_out), .S(OPCODE[3]), .Q(R));
  assign bit_extender_1_out = {{7{1'b0}}, or_1_out};  // Bit_Extender bit_extender_1

  // Other names for the same wires on the sheet: OP0 = OPCODE[0]; OP1 = OPCODE[1]; OP2 = OPCODE[2]
endmodule

module Counter8 (
  input  ENABLE,
  input  CLK,
  output [7:0] COUNT
);

  wire and_1_out, and_2_out, and_3_out, and_4_out, and_5_out, and_6_out, and_7_out;

  J_K_Flip_Flop j_k_ff_1 (.J(ENABLE), .K(ENABLE), .clk(CLK), .Q(COUNT[0]));  // open: Qn, preset, reset
  and and_1 (and_1_out, ENABLE, COUNT[0]);
  J_K_Flip_Flop j_k_ff_2 (.J(and_1_out), .K(and_1_out), .clk(CLK), .Q(COUNT[1]));  // open: Qn, preset, reset
  and and_2 (and_2_out, and_1_out, COUNT[1]);
  J_K_Flip_Flop j_k_ff_3 (.J(and_2_out), .K(and_2_out), .clk(CLK), .Q(COUNT[2]));  // open: Qn, preset, reset
  and and_3 (and_3_out, and_2_out, COUNT[2]);
  J_K_Flip_Flop j_k_ff_4 (.J(and_3_out), .K(and_3_out), .clk(CLK), .Q(COUNT[3]));  // open: Qn, preset, reset
  and and_4 (and_4_out, and_3_out, COUNT[3]);
  J_K_Flip_Flop j_k_ff_5 (.J(and_4_out), .K(and_4_out), .clk(CLK), .Q(COUNT[4]));  // open: Qn, preset, reset
  and and_5 (and_5_out, and_4_out, COUNT[4]);
  J_K_Flip_Flop j_k_ff_6 (.J(and_5_out), .K(and_5_out), .clk(CLK), .Q(COUNT[5]));  // open: Qn, preset, reset
  and and_6 (and_6_out, and_5_out, COUNT[5]);
  J_K_Flip_Flop j_k_ff_7 (.J(and_6_out), .K(and_6_out), .clk(CLK), .Q(COUNT[6]));  // open: Qn, preset, reset
  and and_7 (and_7_out, and_6_out, COUNT[6]);
  J_K_Flip_Flop j_k_ff_8 (.J(and_7_out), .K(and_7_out), .clk(CLK), .Q(COUNT[7]));  // open: Qn, preset, reset
endmodule

module Register8 (
  input  [7:0] D_in,
  input  WH,
  input  WL,
  input  CLK,
  output [7:0] D_out
);

  wire controlled_buffer_1_out, controlled_buffer_2_out, controlled_buffer_3_out, controlled_buffer_4_out,
       controlled_buffer_5_out, controlled_buffer_6_out, controlled_buffer_7_out, controlled_buffer_8_out;

  assign controlled_buffer_1_out = WH ? D_in[7] : 1'bz;  // Controlled_Buffer controlled_buffer_1
  D_Flip_Flop d_ff_1 (.D(controlled_buffer_1_out), .clk(CLK), .Q(D_out[7]));  // open: Qn, preset, reset
  assign controlled_buffer_2_out = WH ? D_in[6] : 1'bz;  // Controlled_Buffer controlled_buffer_2
  D_Flip_Flop d_ff_2 (.D(controlled_buffer_2_out), .clk(CLK), .Q(D_out[6]));  // open: Qn, preset, reset
  assign controlled_buffer_3_out = WH ? D_in[5] : 1'bz;  // Controlled_Buffer controlled_buffer_3
  D_Flip_Flop d_ff_3 (.D(controlled_buffer_3_out), .clk(CLK), .Q(D_out[5]));  // open: Qn, preset, reset
  assign controlled_buffer_4_out = WH ? D_in[4] : 1'bz;  // Controlled_Buffer controlled_buffer_4
  D_Flip_Flop d_ff_4 (.D(controlled_buffer_4_out), .clk(CLK), .Q(D_out[4]));  // open: Qn, preset, reset
  assign controlled_buffer_5_out = WL ? D_in[3] : 1'bz;  // Controlled_Buffer controlled_buffer_5
  D_Flip_Flop d_ff_5 (.D(controlled_buffer_5_out), .clk(CLK), .Q(D_out[3]));  // open: Qn, preset, reset
  assign controlled_buffer_6_out = WL ? D_in[2] : 1'bz;  // Controlled_Buffer controlled_buffer_6
  D_Flip_Flop d_ff_6 (.D(controlled_buffer_6_out), .clk(CLK), .Q(D_out[2]));  // open: Qn, preset, reset
  assign controlled_buffer_7_out = WL ? D_in[1] : 1'bz;  // Controlled_Buffer controlled_buffer_7
  D_Flip_Flop d_ff_7 (.D(controlled_buffer_7_out), .clk(CLK), .Q(D_out[1]));  // open: Qn, preset, reset
  assign controlled_buffer_8_out = WL ? D_in[0] : 1'bz;  // Controlled_Buffer controlled_buffer_8
  D_Flip_Flop d_ff_8 (.D(controlled_buffer_8_out), .clk(CLK), .Q(D_out[0]));  // open: Qn, preset, reset
endmodule

module CPU (
  input  CLK,
  input  [7:0] INSTRUCT,
  output [7:0] A,
  output [7:0] B,
  output [7:0] C,
  output [7:0] ADDR,
  output [7:0] out_7
);

  wire A_WH, A_WL, and_1_out, and_2_out, and_3_out, and_5_out, and_6_out, and_7_out, B_WH, B_WL, C_WH, C_WL,
       D_WH, D_WL, PC_ENABLE, Y_W;
  wire [7:0] Operand0, Operand1, Operand2, Y_D;

  and and_1 (and_1_out, INSTRUCT[6], ~INSTRUCT[5], ~INSTRUCT[4]);  // AND_Gate
  and and_2 (and_2_out, ~INSTRUCT[6], INSTRUCT[5], ~INSTRUCT[4]);  // AND_Gate
  and and_3 (and_3_out, INSTRUCT[6], ~INSTRUCT[5], INSTRUCT[4]);  // AND_Gate
  Register8 RegiA (.D_in(A), .WH(A_WH), .WL(A_WL), .CLK(CLK), .D_out(A));
  Register8 RegiB (.D_in(A), .WH(B_WH), .WL(B_WL), .CLK(CLK), .D_out(A));
  Register8 RegiC (.D_in(C), .WH(C_WH), .WL(C_WL), .CLK(CLK), .D_out(C));
  Register8 RegiD (.D_in(out_7), .WH(D_WH), .WL(D_WL), .CLK(CLK), .D_out(out_7));
  or or_1 (A_WL, and_1_out, and_2_out);
  or or_2 (A_WH, and_2_out, and_3_out);
  MUX8 mux8_1 (.D0(Y_D), .D1({INSTRUCT[3:0], INSTRUCT[3:0]}), .S(INSTRUCT[6]), .Q(A));
  Counter PCTR (.up(1'b1), .count(PC_ENABLE), .clk(CLK), .Q(ADDR));  // open: clr, load, D, carry
  or or_3 (PC_ENABLE, INSTRUCT[0], INSTRUCT[1], INSTRUCT[2], INSTRUCT[3], INSTRUCT[4], INSTRUCT[5], INSTRUCT[6], INSTRUCT[7]);
  and and_4 (Y_W, ~INSTRUCT[7], ~INSTRUCT[6], ~INSTRUCT[5], INSTRUCT[4]);  // AND_Gate
  and and_5 (and_5_out, INSTRUCT[6], INSTRUCT[5], ~INSTRUCT[4]);  // AND_Gate
  and and_6 (and_6_out, ~INSTRUCT[6], INSTRUCT[5], INSTRUCT[4]);  // AND_Gate
  and and_7 (and_7_out, INSTRUCT[6], INSTRUCT[5], INSTRUCT[4]);
  ALU8 alu8_1 (.X(Operand0), .Y(Operand1), .OPCODE(INSTRUCT[3:0]), .R(Operand2));  // open: STATUS
  or or_4 (B_WL, and_5_out, and_6_out);
  or or_5 (B_WH, and_6_out, and_7_out);

  assign B = A;

  // Other names for the same wires on the sheet: A_D[7:0] = A; B_D[7:0] = A; C_D[7:0] = C; Clock = CLK;
  //   D_D[7:0] = out_7; DL[3:0] = INSTRUCT[3:0]; INST0 = INSTRUCT[0]; OPCODE[3:0] = INSTRUCT[3:0];
  //   INST1 = INSTRUCT[1]; INST2 = INSTRUCT[2]; INST3 = INSTRUCT[3]; INST4 = INSTRUCT[4]; INST5 = INSTRUCT[5];
  //   INST6 = INSTRUCT[6]; INST7 = INSTRUCT[7]
endmodule

module Main (
  output [7:0] out_1,
  output [7:0] out_2,
  output [7:0] out_3
);

  wire clock_1_out;
  wire [7:0] cpu_1_addr, rom_1_data;

  ROM rom_1 (.addr(cpu_1_addr), .data(rom_1_data));
  Clock clock_1 (.out(clock_1_out));
  CPU cpu_1 (
    .CLK(clock_1_out), .INSTRUCT(rom_1_data), .A(out_1), .B(out_2), .C(out_3), .ADDR(cpu_1_addr));  // open: out_7

  // Notes on the sheet:
  //   contents of rom_1 (hex, n*v repeats v):
  //   4a 5a 6a 7a 19
endmodule
